// Logisim project control.circ as structural Verilog: 1 circuit, main circuit main
module main (
  input  fisrBit,
  input  equalOutput,
  input  go,
  input  Clock,
  output loadMultiplicand,
  output loadProduct,
  output LoadMultiplier,
  output SelectMultiplier,
  output SelectProduct,
  output Add,
  output selectCounter,
  output loadCounter
);

  wire _011_out, and_1_out, and_2_out, and_3_out, and_4_out, and_5_out, and_6_out, not_1_out, not_2_out,
       not_3_out, not_4_out, not_5_out, not_6_out, not_7_out, not_8_out, not_9_out, not_10_out, not_11_out,
       not_12_out, not_13_out, not_14_out, not_15_out, not_16_out, not_17_out, not_18_out;
  wire [2:0] n0_out, register_1_q;

  Register #(.width(3)) register_1 (.D(n0_out), .en(1'b1), .Q(register_1_q), .clk(Clock));  // open: clr
  not not_1 (not_1_out, register_1_q[2]);
  not not_2 (not_2_out, register_1_q[0]);
  not not_3 (not_3_out, fisrBit);
  not not_4 (not_4_out, register_1_q[2]);
  not not_5 (not_5_out, register_1_q[1]);
  not not_6 (not_6_out, register_1_q[0]);
  not not_7 (not_7_out, register_1_q[2]);
  not not_8 (not_8_out, register_1_q[1]);
  not not_9 (not_9_out, register_1_q[0]);
  not not_10 (not_10_out, fisrBit);
  not not_11 (not_11_out, register_1_q[1]);
  not not_12 (not_12_out, equalOutput);
  not not_13 (not_13_out, register_1_q[2]);
  and and_1 (and_1_out, not_4_out, register_1_q[1], not_6_out, not_3_out);
  and N2 (n0_out[2], not_1_out, register_1_q[1], not_2_out, fisrBit);
  and and_2 (and_2_out, not_7_out, register_1_q[0], not_8_out);
  and and_3 (and_3_out, not_7_out, register_1_q[1], not_9_out, not_10_out);
  and and_4 (and_4_out, register_1_q[2], not_11_out, not_9_out, not_12_out);
  and and_5 (and_5_out, not_13_out, register_1_q[1], register_1_q[0], not_12_out);
  and and_6 (and_6_out, not_4_out, not_5_out, not_6_out, go);
  or N1 (n0_out[1], and_2_out, and_3_out, and_4_out, and_5_out);
  or n0 (n0_out[0], and_1_out, and_6_out);
  not not_14 (not_14_out, register_1_q[2]);
  not not_15 (not_15_out, register_1_q[1]);
  not not_16 (not_16_out, register_1_q[1]);
  not not_17 (not_17_out, register_1_q[0]);
  not not_18 (not_18_out, register_1_q[2]);
  and _001 (loadMultiplicand, not_14_out, not_15_out, register_1_q[0]);
  and _100 (Add, register_1_q[2], not_16_out, not_17_out);
  and _011 (_011_out, not_18_out, register_1_q[1], register_1_q[0]);
  or or_1 (loadCounter, loadMultiplicand, Add, _011_out);
  or or_2 (SelectProduct, Add, _011_out);

  assign LoadMultiplier = loadCounter;
  assign loadProduct = loadCounter;
  assign selectCounter = loadMultiplicand;
  assign SelectMultiplier = loadMultiplicand;
endmodule
