// Logisim project datapath.circ as structural Verilog: 6 circuits, main circuit main
module main (
  input  [31:0] Multiplicand,
  input  loadMultiplicand,
  input  add,
  input  selectProduct,
  input  loadProduct,
  input  selectMultiplier,
  input  Clock,
  input  [31:0] Multiplier,
  input  loadMultiplier,
  input  selectCounter,
  input  loadCounter,
  output [31:0] OutputProduct,
  output FirstBit,
  output [31:0] OutputMultiplayer,
  output equalOutput
);

  wire multiplexer_5_out, \n32bıtadder_1_cout ;
  wire [5:0] multiplexer_1_out, \n6bıtadder_1_sum , register_1_q;
  wire [31:0] multiplexer_2_out, multiplexer_3_out, multiplexer_4_out, Multiplicand_q, \n32bıtadder_1_out_4 ,
       \shıfter_1_multiplieroutput , \shıfter_1_productoutput ;

  Multiplexer #(.width(6), .enable("false")) multiplexer_1 (
    .in0(\n6bıtadder_1_sum ), .in1({6{1'b0}}), .out(multiplexer_1_out), .sel(selectCounter));
  Register #(.width(32)) u_Multiplicand (
    .D(Multiplicand), .en(loadMultiplicand), .Q(Multiplicand_q), .clk(Clock));  // open: clr
  Register #(.width(6)) register_1 (
    .D(multiplexer_1_out), .en(loadCounter), .Q(register_1_q), .clk(Clock));  // open: clr
  Multiplexer #(.width(32), .enable("false")) multiplexer_2 (
    .in0({32{1'b0}}), .in1(\shıfter_1_productoutput ), .out(multiplexer_2_out), .sel(selectProduct));
  \_32BıtAdder  \u_32bıtadder_1  (
    .A(OutputProduct), .B(Multiplicand_q), .out_4(\n32bıtadder_1_out_4 ), .Cout(\n32bıtadder_1_cout ));
  \_6BıtAdder  \u_6bıtadder_1  (.in_1(6'b000001), .in_2(register_1_q), .Sum(\n6bıtadder_1_sum ));  // open: Cout
  Register #(.width(32)) Product (
    .D(multiplexer_2_out), .en(loadProduct), .Q(OutputProduct), .clk(Clock));  // open: clr
  \ısEqual  \u_ısequal_1  (.input1(register_1_q), .input2(6'b011111), .\output (equalOutput));
  Multiplexer #(.width(32), .enable("false")) multiplexer_3 (
    .in0(OutputProduct), .in1(\n32bıtadder_1_out_4 ), .out(multiplexer_3_out), .sel(add));
  Multiplexer #(.width(32), .enable("false")) multiplexer_4 (
    .in0(\shıfter_1_multiplieroutput ), .in1(Multiplier), .out(multiplexer_4_out), .sel(selectMultiplier));
  Multiplexer #(.enable("false")) multiplexer_5 (
    .in0(1'b0), .in1(\n32bıtadder_1_cout ), .out(multiplexer_5_out), .sel(add));
  \Shıfter  \shıfter_1  (
    .Cout(multiplexer_5_out), .Product(multiplexer_3_out), .Multiplier({OutputMultiplayer[31:1], FirstBit}),
    .ProductOutput(\shıfter_1_productoutput ), .MultiplierOutput(\shıfter_1_multiplieroutput ));
  Register #(.width(32)) u_Multiplier (
    .D(multiplexer_4_out), .en(loadMultiplier), .Q({OutputMultiplayer[31:1], FirstBit}), .clk(Clock));  // open: clr

  assign OutputMultiplayer[0] = FirstBit;
endmodule

module \_1BıtAdder  (
  input  A,
  input  B,
  input  Cin,
  output SUM,
  output Cout
);

  wire and_1_out, and_2_out, xor_1_out;

  xor xor_1 (xor_1_out, A, B);
  xor xor_2 (SUM, xor_1_out, Cin);
  and and_1 (and_1_out, Cin, xor_1_out);
  and and_2 (and_2_out, A, B);
  or or_1 (Cout, and_1_out, and_2_out);
endmodule

module \_32BıtAdder  (
  input  [31:0] A,
  input  [31:0] B,
  output Cout,
  output [31:0] out_4
);

  wire \n1bıtadder_1_cout , \n1bıtadder_2_cout , \n1bıtadder_3_cout , \n1bıtadder_4_cout ,
       \n1bıtadder_5_cout , \n1bıtadder_6_cout , \n1bıtadder_7_cout , \n1bıtadder_8_cout ,
       \n1bıtadder_9_cout , \n1bıtadder_10_cout , \n1bıtadder_11_cout , \n1bıtadder_12_cout ,
       \n1bıtadder_13_cout , \n1bıtadder_14_cout , \n1bıtadder_15_cout , \n1bıtadder_16_cout ,
       \n1bıtadder_17_cout , \n1bıtadder_18_cout , \n1bıtadder_19_cout , \n1bıtadder_20_cout ,
       \n1bıtadder_21_cout , \n1bıtadder_22_cout , \n1bıtadder_23_cout , \n1bıtadder_24_cout ,
       \n1bıtadder_25_cout , \n1bıtadder_26_cout , \n1bıtadder_27_cout , \n1bıtadder_28_cout ,
       \n1bıtadder_29_cout , \n1bıtadder_30_cout , \n1bıtadder_31_cout ;

  \_1BıtAdder  \u_1bıtadder_1  (.A(A[0]), .B(B[0]), .Cin(1'b0), .SUM(out_4[0]), .Cout(\n1bıtadder_1_cout ));
  \_1BıtAdder  \u_1bıtadder_2  (
    .A(A[1]), .B(B[1]), .Cin(\n1bıtadder_1_cout ), .SUM(out_4[1]), .Cout(\n1bıtadder_2_cout ));
  \_1BıtAdder  \u_1bıtadder_3  (
    .A(A[2]), .B(B[2]), .Cin(\n1bıtadder_2_cout ), .SUM(out_4[2]), .Cout(\n1bıtadder_3_cout ));
  \_1BıtAdder  \u_1bıtadder_4  (
    .A(A[3]), .B(B[3]), .Cin(\n1bıtadder_3_cout ), .SUM(out_4[3]), .Cout(\n1bıtadder_4_cout ));
  \_1BıtAdder  \u_1bıtadder_5  (
    .A(A[4]), .B(B[4]), .Cin(\n1bıtadder_4_cout ), .SUM(out_4[4]), .Cout(\n1bıtadder_5_cout ));
  \_1BıtAdder  \u_1bıtadder_6  (
    .A(A[5]), .B(B[5]), .Cin(\n1bıtadder_5_cout ), .SUM(out_4[5]), .Cout(\n1bıtadder_6_cout ));
  \_1BıtAdder  \u_1bıtadder_7  (
    .A(A[6]), .B(B[6]), .Cin(\n1bıtadder_6_cout ), .SUM(out_4[6]), .Cout(\n1bıtadder_7_cout ));
  \_1BıtAdder  \u_1bıtadder_8  (
    .A(A[7]), .B(B[7]), .Cin(\n1bıtadder_7_cout ), .SUM(out_4[7]), .Cout(\n1bıtadder_8_cout ));
  \_1BıtAdder  \u_1bıtadder_9  (
    .A(A[8]), .B(B[8]), .Cin(\n1bıtadder_8_cout ), .SUM(out_4[8]), .Cout(\n1bıtadder_9_cout ));
  \_1BıtAdder  \u_1bıtadder_10  (
    .A(A[9]), .B(B[9]), .Cin(\n1bıtadder_9_cout ), .SUM(out_4[9]), .Cout(\n1bıtadder_10_cout ));
  \_1BıtAdder  \u_1bıtadder_11  (
    .A(A[10]), .B(B[10]), .Cin(\n1bıtadder_10_cout ), .SUM(out_4[10]), .Cout(\n1bıtadder_11_cout ));
  \_1BıtAdder  \u_1bıtadder_12  (
    .A(A[11]), .B(B[11]), .Cin(\n1bıtadder_11_cout ), .SUM(out_4[11]), .Cout(\n1bıtadder_12_cout ));
  \_1BıtAdder  \u_1bıtadder_13  (
    .A(A[12]), .B(B[12]), .Cin(\n1bıtadder_12_cout ), .SUM(out_4[12]), .Cout(\n1bıtadder_13_cout ));
  \_1BıtAdder  \u_1bıtadder_14  (
    .A(A[13]), .B(B[13]), .Cin(\n1bıtadder_13_cout ), .SUM(out_4[13]), .Cout(\n1bıtadder_14_cout ));
  \_1BıtAdder  \u_1bıtadder_15  (
    .A(A[14]), .B(B[14]), .Cin(\n1bıtadder_14_cout ), .SUM(out_4[14]), .Cout(\n1bıtadder_15_cout ));
  \_1BıtAdder  \u_1bıtadder_16  (
    .A(A[15]), .B(B[15]), .Cin(\n1bıtadder_15_cout ), .SUM(out_4[15]), .Cout(\n1bıtadder_16_cout ));
  \_1BıtAdder  \u_1bıtadder_17  (
    .A(A[16]), .B(B[16]), .Cin(\n1bıtadder_16_cout ), .SUM(out_4[16]), .Cout(\n1bıtadder_17_cout ));
  \_1BıtAdder  \u_1bıtadder_18  (
    .A(A[17]), .B(B[17]), .Cin(\n1bıtadder_17_cout ), .SUM(out_4[17]), .Cout(\n1bıtadder_18_cout ));
  \_1BıtAdder  \u_1bıtadder_19  (
    .A(A[18]), .B(B[18]), .Cin(\n1bıtadder_18_cout ), .SUM(out_4[18]), .Cout(\n1bıtadder_19_cout ));
  \_1BıtAdder  \u_1bıtadder_20  (
    .A(A[19]), .B(B[19]), .Cin(\n1bıtadder_19_cout ), .SUM(out_4[19]), .Cout(\n1bıtadder_20_cout ));
  \_1BıtAdder  \u_1bıtadder_21  (
    .A(A[20]), .B(B[20]), .Cin(\n1bıtadder_20_cout ), .SUM(out_4[20]), .Cout(\n1bıtadder_21_cout ));
  \_1BıtAdder  \u_1bıtadder_22  (
    .A(A[21]), .B(B[21]), .Cin(\n1bıtadder_21_cout ), .SUM(out_4[21]), .Cout(\n1bıtadder_22_cout ));
  \_1BıtAdder  \u_1bıtadder_23  (
    .A(A[22]), .B(B[22]), .Cin(\n1bıtadder_22_cout ), .SUM(out_4[22]), .Cout(\n1bıtadder_23_cout ));
  \_1BıtAdder  \u_1bıtadder_24  (
    .A(A[23]), .B(B[23]), .Cin(\n1bıtadder_23_cout ), .SUM(out_4[23]), .Cout(\n1bıtadder_24_cout ));
  \_1BıtAdder  \u_1bıtadder_25  (
    .A(A[24]), .B(B[24]), .Cin(\n1bıtadder_24_cout ), .SUM(out_4[24]), .Cout(\n1bıtadder_25_cout ));
  \_1BıtAdder  \u_1bıtadder_26  (
    .A(A[25]), .B(B[25]), .Cin(\n1bıtadder_25_cout ), .SUM(out_4[25]), .Cout(\n1bıtadder_26_cout ));
  \_1BıtAdder  \u_1bıtadder_27  (
    .A(A[26]), .B(B[26]), .Cin(\n1bıtadder_26_cout ), .SUM(out_4[26]), .Cout(\n1bıtadder_27_cout ));
  \_1BıtAdder  \u_1bıtadder_28  (
    .A(A[27]), .B(B[27]), .Cin(\n1bıtadder_27_cout ), .SUM(out_4[27]), .Cout(\n1bıtadder_28_cout ));
  \_1BıtAdder  \u_1bıtadder_29  (
    .A(A[28]), .B(B[28]), .Cin(\n1bıtadder_28_cout ), .SUM(out_4[28]), .Cout(\n1bıtadder_29_cout ));
  \_1BıtAdder  \u_1bıtadder_30  (
    .A(A[29]), .B(B[29]), .Cin(\n1bıtadder_29_cout ), .SUM(out_4[29]), .Cout(\n1bıtadder_30_cout ));
  \_1BıtAdder  \u_1bıtadder_31  (
    .A(A[30]), .B(B[30]), .Cin(\n1bıtadder_30_cout ), .SUM(out_4[30]), .Cout(\n1bıtadder_31_cout ));
  \_1BıtAdder  \u_1bıtadder_32  (.A(A[31]), .B(B[31]), .Cin(\n1bıtadder_31_cout ), .SUM(out_4[31]), .Cout(Cout));
endmodule

module \_6BıtAdder  (
  input  [5:0] in_1,
  input  [5:0] in_2,
  output Cout,
  output [5:0] Sum
);

  wire \n1bıtadder_1_cout , \n1bıtadder_2_cout , \n1bıtadder_3_cout , \n1bıtadder_4_cout ,
       \n1bıtadder_5_cout ;

  \_1BıtAdder  \u_1bıtadder_1  (.A(in_2[0]), .B(in_1[0]), .Cin(1'b0), .SUM(Sum[0]), .Cout(\n1bıtadder_1_cout ));
  \_1BıtAdder  \u_1bıtadder_2  (
    .A(in_2[1]), .B(in_1[1]), .Cin(\n1bıtadder_1_cout ), .SUM(Sum[1]), .Cout(\n1bıtadder_2_cout ));
  \_1BıtAdder  \u_1bıtadder_3  (
    .A(in_2[2]), .B(in_1[2]), .Cin(\n1bıtadder_2_cout ), .SUM(Sum[2]), .Cout(\n1bıtadder_3_cout ));
  \_1BıtAdder  \u_1bıtadder_4  (
    .A(in_2[3]), .B(in_1[3]), .Cin(\n1bıtadder_3_cout ), .SUM(Sum[3]), .Cout(\n1bıtadder_4_cout ));
  \_1BıtAdder  \u_1bıtadder_5  (
    .A(in_2[4]), .B(in_1[4]), .Cin(\n1bıtadder_4_cout ), .SUM(Sum[4]), .Cout(\n1bıtadder_5_cout ));
  \_1BıtAdder  \u_1bıtadder_6  (.A(in_2[5]), .B(in_1[5]), .Cin(\n1bıtadder_5_cout ), .SUM(Sum[5]), .Cout(Cout));
endmodule

module \Shıfter  (
  input  Cout,
  input  [31:0] Product,
  input  [31:0] Multiplier,
  output [31:0] ProductOutput,
  output [31:0] MultiplierOutput
);


  assign MultiplierOutput = {Product[0], Multiplier[31:1]};
  assign ProductOutput = {Cout, Product[31:1]};
endmodule

module \ısEqual  (
  input  [5:0] input1,
  input  [5:0] input2,
  output \output 
);

  wire xnor_1_out, xnor_2_out, xnor_3_out, xnor_4_out, xnor_5_out, xnor_6_out;

  xnor xnor_1 (xnor_1_out, input1[0], input2[0]);
  xnor xnor_2 (xnor_2_out, input1[1], input2[1]);
  xnor xnor_3 (xnor_3_out, input1[2], input2[2]);
  xnor xnor_4 (xnor_4_out, input1[3], input2[3]);
  xnor xnor_5 (xnor_5_out, input1[4], input2[4]);
  xnor xnor_6 (xnor_6_out, input1[5], input2[5]);
  and and_1 (\output , xnor_1_out, xnor_2_out, xnor_3_out, xnor_4_out, xnor_5_out, xnor_6_out);
endmodule
