// Logisim project mult32.circ as structural Verilog: 1 circuit, main circuit main
module main (
  input  Start,
  input  [31:0] multiplier,
  input  [31:0] multiplicand,
  output [31:0] out_4,
  output [31:0] out_5
);

  wire clock_1_out, main_1_add, main_1_loadcounter, main_1_loadmultiplicand, main_1_loadmultiplier,
       main_1_loadproduct, main_1_selectcounter, main_1_selectmultiplier, main_1_selectproduct,
       main_2_equaloutput, main_2_firstbit;

  control_main main_1 (
    .Clock(clock_1_out), .go(Start), .equalOutput(main_2_equaloutput), .fisrBit(main_2_firstbit),
    .loadMultiplicand(main_1_loadmultiplicand), .loadProduct(main_1_loadproduct),
    .LoadMultiplier(main_1_loadmultiplier), .SelectMultiplier(main_1_selectmultiplier),
    .SelectProduct(main_1_selectproduct), .Add(main_1_add), .selectCounter(main_1_selectcounter),
    .loadCounter(main_1_loadcounter));
  datapath_main main_2 (
    .Multiplicand(multiplicand), .loadMultiplicand(main_1_loadmultiplicand), .add(main_1_add),
    .selectProduct(main_1_selectproduct), .loadProduct(main_1_loadproduct), .Clock(clock_1_out),
    .Multiplier(multiplier), .loadMultiplier(main_1_loadmultiplier), .loadCounter(main_1_loadcounter),
    .selectCounter(main_1_selectcounter), .selectMultiplier(main_1_selectmultiplier),
    .FirstBit(main_2_firstbit), .OutputProduct(out_4), .OutputMultiplayer(out_5),
    .equalOutput(main_2_equaloutput));
  Clock clock_1 (.out(clock_1_out));

  // Notes on the sheet:
  //   RESULT
endmodule
